# Fritzing sketch cablage_appinventor (saved by Fritzing 0.9.2b)

parts:
  Composant1 = Arduino Uno (Rev3)
  Composant3 = Bluetooth HC-05 Macho
  LED1 = LED - 5mm [color="Red (633nm)" package="5 mm [THT]"]

nets:
  N1: Composant1.D9_PWM, LED1.anode
  GND: Composant1.GND, Composant3.GND, LED1.cathode
  N2: Composant1.D0/RX, Composant3.TXD
  N3: Composant1.D1/TX, Composant3.RXD
  3V3: Composant1.3V3, Composant3.VCC
